# Fritzing sketch BoxA_shield_v1 (saved by Fritzing 0.9.2b)
circuit board: 7.05793cm x 5.33763cm
breadboards: 1

parts:
  motor1 = DC Motor
  LED1 = Super Flux RGB LED (com. cathode)
  M1 = Header 2 [package=screwterminal-3.5mm-2_lock]
  S1 = Header 4 [package=jst-4-pth]
  L1 = Header 4 [package=jst-4-pth]
  Part1 = Arduino Uno (Rev3)
  V = Header 4 [package=jst-4-pth]
  Part2 = HC-SR04 Ultrasonic Rangemeter
  Q2 = TRANSISTOR_NPN [package=to-92-ammo]
  R3 = Resistor [tolerance=±5% resistance=270 package="1206 [SMD]"]
  D2 = Rectifier Diode [part_number=1N4001 package="300 mil [THT]"]
  C1 = Capacitor Polarized [package=cpol-radial-1000uf-25v]

nets:
  N1: motor1.pin_1, M1.2, Part1.VIN, V.1, D2.cathode, C1.+
  N2: motor1.pin_2, M1.1, Q2.C, D2.anode, C1.-
  N3: LED1.red_anode, L1.2, Part1.D11_PWM/MOSI
  N4: LED1.blue_anode, L1.4, Part1.D9_PWM
  N5: LED1.green_anode, L1.3, Part1.D10_PWM/SS
  GND: LED1.common_cathode, S1.1, L1.1, Part1.GND, V.2, Part2.GND, Q2.E
  N6: S1.2, Part1.D13/SCK, Part2.Trig
  N7: S1.3, Part1.D12/MISO, Part2.Echo
  5V: S1.4, Part1.5V, V.4, Part2.VCC
  N8: Part1.D3_PWM, R3.Pin_0
  N9: Q2.B, R3.Pin_1

notes:
  ORANGE = 5V
  RED = 12V
  ATENÇÂO:
  trigger pin e echo pin são ao contrário do SRF05!!!!!
