# Fritzing sketch BoxB_shield_v1 (saved by Fritzing 0.9.2b)
circuit board: 6.18325cm x 5.34513cm
breadboards: 1

parts:
  motor1 = DC Motor
  motor2 = DC Motor
  LED2 = Super Flux RGB LED (com. cathode)
  Rgreen = Trimmer Potentiometer [maximum_resistance=100kΩ package=THT]
  Rblue = Trimmer Potentiometer [maximum_resistance=100kΩ package=THT]
  M1 = Header 2 [package=screwterminal-3.5mm-2_lock]
  M2 = Header 2 [package=screwterminal-3.5mm-2_lock]
  LED1 = Super Flux RGB LED (com. cathode)
  S1 = Header 4 [package=jst-4-pth]
  L1 = Header 4 [package=jst-4-pth]
  L2 = Header 4 [package=jst-4-pth]
  ARDUINO = Arduino Uno (Rev3)
  SR04 = HC-SR04 Ultrasonic Rangemeter
  V = Header 4 [package=jst-4-pth]
  R1 = Resistor [tolerance=±5% resistance=270 package="1206 [SMD]"]
  C1 = Capacitor Polarized [package=cpol-radial-1000uf-25v]
  D1 = Rectifier Diode [part_number=1N4001 package="300 mil [THT]"]
  Q1 = TRANSISTOR_NPN [package=to-92-ammo]
  Q2 = TRANSISTOR_NPN [package=to-92-ammo]
  R2 = Resistor [tolerance=±5% resistance=270 package="1206 [SMD]"]
  D2 = Rectifier Diode [part_number=1N4001 package="300 mil [THT]"]
  C2 = Capacitor Polarized [package=cpol-radial-1000uf-25v]
  Rred = Trimmer Potentiometer [maximum_resistance=100kΩ package=THT]

nets:
  N1: motor1.pin_1, motor2.pin_1, M1.2, M2.2, ARDUINO.VIN, V.4, C1.+, D1.cathode, D2.cathode, C2.+
  N2: motor1.pin_2, M1.1, C1.-, D1.anode, Q1.C
  N3: motor2.pin_2, M2.1, Q2.C, D2.anode, C2.-
  N4: LED2.red_anode, L2.2, Rred.leg2
  N5: LED2.blue_anode, Rblue.leg2, L2.4
  N6: LED2.green_anode, Rgreen.leg2, L2.3
  GND: LED2.common_cathode, LED1.common_cathode, S1.1, L1.1, L2.1, ARDUINO.GND, SR04.GND, V.2, Q1.E, Q2.E
  N7: Rgreen.wiper, Rblue.wiper, ARDUINO.D6_PWM, Rred.wiper
  N8: LED1.red_anode, L1.2, ARDUINO.D11_PWM/MOSI
  N9: LED1.blue_anode, L1.4, ARDUINO.D9_PWM
  N10: LED1.green_anode, L1.3, ARDUINO.D10_PWM/SS
  N11: S1.2, ARDUINO.D13/SCK, SR04.Trig
  N12: S1.3, ARDUINO.D12/MISO, SR04.Echo
  5V: S1.4, ARDUINO.5V, SR04.VCC, V.1
  N13: ARDUINO.D3_PWM, R1.Pin_0
  N14: ARDUINO.D5_PWM, R2.Pin_0
  N15: R1.Pin_1, Q1.B
  N16: Q2.B, R2.Pin_1

notes:
  ORANGE = 5V
  RED = 12V
  ATENÇÂO:
  trigger pin e echo pin são ao contrário do SRF05!!!!!
