# Fritzing sketch BoxC_shield_v1 (saved by Fritzing 0.9.2b)
circuit board: 7.17039cm x 5.31967cm
breadboards: 1

parts:
  motor1 = DC Motor
  motor2 = DC Motor
  motor3 = DC Motor
  LED1 = Super Flux RGB LED (com. cathode)
  Q2 = TRANSISTOR_NPN [package=to-92-ammo]
  Q3 = TRANSISTOR_NPN [package=to-92-ammo]
  R2 = Resistor [tolerance=±5% resistance=270 package="1206 [SMD]"]
  R3 = Resistor [tolerance=±5% resistance=270 package="1206 [SMD]"]
  D2 = Rectifier Diode [part_number=1N4001 package="300 mil [THT]"]
  D3 = Rectifier Diode [part_number=1N4001 package="300 mil [THT]"]
  C2 = Capacitor Polarized [package=cpol-radial-1000uf-25v]
  C3 = Capacitor Polarized [package=cpol-radial-1000uf-25v]
  M1 = Header 2 [package=screwterminal-3.5mm-2_lock]
  M2 = Header 2 [package=screwterminal-3.5mm-2_lock]
  M3 = Header 2 [package=screwterminal-3.5mm-2_lock]
  S1 = Header 4 [package=jst-4-pth]
  L1 = Header 4 [package=jst-4-pth]
  Vpin = Header 2 [package=jst-2-pth]
  ARDUINO = Arduino Uno (Rev3)
  SR04 = HC-SR04 Ultrasonic Rangemeter
  Q1 = TRANSISTOR_NPN [package=to-92-ammo]
  R1 = Resistor [tolerance=±5% resistance=270 package="1206 [SMD]"]
  D1 = Rectifier Diode [part_number=1N4001 package="300 mil [THT]"]
  C1 = Capacitor Polarized [package=cpol-radial-1000uf-25v]

nets:
  5V: motor1.pin_1, motor2.pin_1, motor3.pin_1, D2.cathode, D3.cathode, C2.+, C3.+, M1.2, M2.2, M3.2, S1.4, Vpin.2, ARDUINO.5V, SR04.VCC, D1.cathode, C1.+
  N1: motor1.pin_2, M1.1, Q1.C, D1.anode, C1.-
  N2: motor2.pin_2, Q2.C, D2.anode, C2.-, M2.1
  N3: motor3.pin_2, Q3.C, D3.anode, C3.-, M3.1
  N4: LED1.red_anode, L1.2, ARDUINO.D11_PWM/MOSI
  N5: LED1.blue_anode, L1.4, ARDUINO.D9_PWM
  N6: LED1.green_anode, L1.3, ARDUINO.D10_PWM/SS
  GND: LED1.common_cathode, Q2.E, Q3.E, S1.1, L1.1, Vpin.1, ARDUINO.GND, SR04.GND, Q1.E
  N7: Q2.B, R2.Pin_1
  N8: Q3.B, R3.Pin_1
  N9: R2.Pin_0, ARDUINO.D5_PWM
  N10: R3.Pin_0, ARDUINO.D3_PWM
  N11: S1.2, ARDUINO.D13/SCK, SR04.Trig
  N12: S1.3, ARDUINO.D12/MISO, SR04.Echo
  N13: ARDUINO.D6_PWM, R1.Pin_0
  N14: Q1.B, R1.Pin_1
