# Fritzing sketch BoxD_shield_v1 (saved by Fritzing 0.9.2b)
circuit board: 6.88728cm x 5.36919cm
breadboards: 1

parts:
  LED2 = Super Flux RGB LED (com. cathode)
  LED1 = Super Flux RGB LED (com. cathode)
  S1 = Header 4 [package=jst-4-pth]
  L2 = Header 4 [package=jst-4-pth]
  L1 = Header 4 [package=jst-4-pth]
  Vpin = Header 2 [package=jst-2-pth]
  RLY = Header 4 [package=jst-4-pth]
  Arduino = Arduino Uno (Rev3) - ICSP
  HC-SR04 = HC-SR04 Ultrasonic Rangemeter

nets:
  N1: LED2.red_anode, L2.2, Arduino.ICSP_MOSI, Arduino.D11_PWM/MOSI
  N2: LED2.blue_anode, L2.4, Arduino.D9_PWM
  N3: LED2.green_anode, L2.3, Arduino.D10_PWM/SS
  GND: LED2.common_cathode, LED1.common_cathode, S1.4, L2.1, L1.1, Vpin.1, RLY.1, Arduino.GND, HC-SR04.GND
  N4: LED1.red_anode, L1.2, Arduino.D6_PWM
  N5: LED1.blue_anode, L1.4, Arduino.D3_PWM
  N6: LED1.green_anode, L1.3, Arduino.D5_PWM
  5V: S1.1, Vpin.2, RLY.4, Arduino.5V, HC-SR04.VCC
  N7: S1.2, Arduino.D8, HC-SR04.Trig
  N8: S1.3, Arduino.D7, HC-SR04.Echo
  N9: RLY.2, Arduino.D2
  N10: RLY.3, Arduino.D4

notes:
  PWM pins:
  2~14
  44~46
  22p
