# Fritzing sketch BoxE_shield_v1 (saved by Fritzing 0.9.2b)
circuit board: 11.2cm x 5.3cm
breadboards: 2

parts:
  motor1 = DC Motor
  SRF1 = SRF05 Ultrasonic Rangefinder
  ARDUINO_MEGA = Arduino Mega 2560 (Rev3)
  motor2 = DC Motor
  motor3 = DC Motor
  motor4 = DC Motor
  LED1 = Super Flux RGB LED (com. cathode)
  LED4 = Super Flux RGB LED (com. cathode)
  Rred = Trimmer Potentiometer [maximum_resistance=100kΩ package=THT]
  Rgreen = Trimmer Potentiometer [maximum_resistance=100kΩ package=THT]
  Rblue = Trimmer Potentiometer [maximum_resistance=100kΩ package=THT]
  Q2 = TRANSISTOR_NPN [package=to-92-ammo]
  Q3 = TRANSISTOR_NPN [package=to-92-ammo]
  Q4 = TRANSISTOR_NPN [package=to-92-ammo]
  R1 = Resistor [tolerance=±5% resistance=270 package="1206 [SMD]"]
  R2 = Resistor [tolerance=±5% resistance=270 package="1206 [SMD]"]
  R3 = Resistor [tolerance=±5% resistance=270 package="1206 [SMD]"]
  R4 = Resistor [tolerance=±5% resistance=270 package="1206 [SMD]"]
  D1 = Rectifier Diode [part_number=1N4001 package="300 mil [THT]"]
  D2 = Rectifier Diode [part_number=1N4001 package="300 mil [THT]"]
  D3 = Rectifier Diode [part_number=1N4001 package="300 mil [THT]"]
  D4 = Rectifier Diode [part_number=1N4001 package="300 mil [THT]"]
  C1 = Capacitor Polarized [package=cpol-radial-1000uf-25v]
  C2 = Capacitor Polarized [package=cpol-radial-1000uf-25v]
  C3 = Capacitor Polarized [package=cpol-radial-1000uf-25v]
  C4 = Capacitor Polarized [package=cpol-radial-1000uf-25v]
  M1 = Header 2 [package=screwterminal-3.5mm-2_lock]
  M2 = Header 2 [package=screwterminal-3.5mm-2_lock]
  M3 = Header 2 [package=screwterminal-3.5mm-2_lock]
  M4 = Header 2 [package=screwterminal-3.5mm-2_lock]
  LED2 = Super Flux RGB LED (com. cathode)
  LED3 = Super Flux RGB LED (com. cathode)
  SRF2 = SRF05 Ultrasonic Rangefinder
  S1 = Header 4 [package=jst-4-pth]
  S2 = Header 4 [package=jst-4-pth]
  L1 = Header 4 [package=jst-4-pth]
  L2 = Header 4 [package=jst-4-pth]
  L3 = Header 4 [package=jst-4-pth]
  L4 = Header 4 [package=jst-4-pth]
  Vpin = Header 2 [package=jst-2-pth]
  Q1 = TRANSISTOR_NPN [package=to-92-ammo]

nets:
  N1: motor1.pin_1, ARDUINO_MEGA.VIN, motor2.pin_1, motor3.pin_1, motor4.pin_1, D1.cathode, D2.cathode, D3.cathode, D4.cathode, C1.+, C2.+, C3.+, C4.+, M1.2, M2.2, M3.2, M4.2
  N2: motor1.pin_2, D1.anode, C1.-, M1.1, Q1.C
  N3: SRF1.5v_Supply, ARDUINO_MEGA.5V, SRF2.5v_Supply, S1.4, S2.4, Vpin.2
  N4: SRF1.Echo_Output, ARDUINO_MEGA.D24, S1.3
  N5: SRF1.Trigger_Input, ARDUINO_MEGA.D22, S1.2
  N6: SRF1.Ground, ARDUINO_MEGA.GND, LED1.common_cathode, Q2.E, Q3.E, Q4.E, LED2.common_cathode, LED3.common_cathode, SRF2.Ground, S1.1, S2.1, L1.1, L2.1, L3.1, L4.1, Vpin.1, Q1.E
  N7: ARDUINO_MEGA.D13_PWM, LED1.red_anode, L1.2
  N8: ARDUINO_MEGA.D12_PWM, LED1.green_anode, L1.3
  N9: ARDUINO_MEGA.D11_PWM, LED1.blue_anode, L1.4
  N10: ARDUINO_MEGA.D10_PWM, LED2.red_anode, L2.2
  N11: ARDUINO_MEGA.D9_PWM, LED2.green_anode, L2.3
  N12: ARDUINO_MEGA.D8_PWM, LED2.blue_anode, L2.4
  N13: ARDUINO_MEGA.D2_PWM, R1.Pin_0
  N14: ARDUINO_MEGA.D3_PWM, R2.Pin_0
  N15: ARDUINO_MEGA.D4_PWM, Rred.wiper, Rgreen.wiper, Rblue.wiper
  N16: ARDUINO_MEGA.D5_PWM, LED3.blue_anode, L3.4
  N17: ARDUINO_MEGA.D6_PWM, LED3.green_anode, L3.3
  N18: ARDUINO_MEGA.D7_PWM, LED3.red_anode, L3.2
  N19: ARDUINO_MEGA.D44, R3.Pin_0
  N20: ARDUINO_MEGA.D46, R4.Pin_0
  N21: ARDUINO_MEGA.D50, SRF2.Trigger_Input, S2.2
  N22: ARDUINO_MEGA.D52, SRF2.Echo_Output, S2.3
  N23: motor2.pin_2, Q2.C, D2.anode, C2.-, M2.1
  N24: motor3.pin_2, Q3.C, D3.anode, C3.-, M3.1
  N25: motor4.pin_2, Q4.C, D4.anode, C4.-, M4.1
  N26: LED4.red_anode, Rred.leg2, L4.2
  N27: LED4.blue_anode, Rblue.leg2, L4.4
  N28: LED4.green_anode, Rgreen.leg2, L4.3
  N29: Q2.B, R2.Pin_1
  N30: Q3.B, R3.Pin_1
  N31: Q4.B, R4.Pin_1
  N32: R1.Pin_1, Q1.B

notes:
  Since Arduino Mega only has 15 pwm pins one of the led's only allows pwm control on 2 pins, leaving one pin with digital control (LOW/HIGH) only!!!!
  PWM pins:
  2~14
  44~46
  ORANGE = 5V
  RED = 12V
  LED4 color control is via potentiometer, where the Arduino only sets it on or off 4
