# Fritzing sketch Magnetics_v1 (saved by Fritzing 0.9.2b)
breadboards: 1

parts:
  motor1 = DC Motor
  M1 = Header 2 [package=screwterminal-3.5mm-2_lock]
  Part1 = Arduino Uno (Rev3)
  Q2 = TRANSISTOR_NPN [package=to-92-ammo]
  R3 = Resistor [tolerance=±5% resistance=270 package="1206 [SMD]"]
  D2 = Rectifier Diode [part_number=1N4001 package="300 mil [THT]"]

nets:
  N1: motor1.pin_1, M1.2, Part1.3V3, D2.cathode
  N2: motor1.pin_2, M1.1, Q2.C, D2.anode
  N3: Part1.D3_PWM, R3.Pin_0
  N4: Part1.GND, Q2.E
  N5: Q2.B, R3.Pin_1
