# Fritzing sketch 555_Spring_Motor_Control_v2 (saved by Fritzing 0.9.2b)
circuit board: 5.2cm x 4.9cm
breadboards: 1

parts:
  555 = General purpose bipolar Timer [package=dil-08]
  C1 = Capacitor [package=cap-pth-small2]
  C2 = Capacitor [package=cap-pth-small2]
  Pot = POT [package=pot_alpha_rv16af-20]
  D1 = Rectifier Diode [part_number=1N4001 package="300 mil [THT]"]
  D2 = Rectifier Diode [part_number=1N4001 package="300 mil [THT]"]
  R2 = Resistor [tolerance=±5% resistance=1k package="0805 [SMD]"]
  C3 = Electrolytic Capacitor [capacitance=1000µF package="300 mil [THT, electrolytic]"]
  motor = DC Motor
  R1 = Resistor [tolerance=±5% resistance=1k package="0805 [SMD]"]
  M = Header 2 [package=screwterminal-3.5mm-2_lock]
  button = Round Pushbutton
  DC_jack = 2.1mm DC Barrel Jack
  V = Header 2 [package=screwterminal-3.5mm-2_lock]
  B = Header 2 [package=screwterminal-3.5mm-2_lock]
  FET = STP16NF06 N-Channel Power MOSFET
  Reg5V = LD33 Low-Dropout Voltage Regulator
  D3 = Rectifier Diode [part_number=1N4001 package="300 mil [THT]"]
  Reg8V = LD33 Low-Dropout Voltage Regulator

nets:
  N1: 555.GND, C1.1, C2.1, DC_jack.sleeve, V.1, FET.source, Reg5V.Vout, Reg8V.Vout
  N2: 555.TRI, 555.TRE, C1.2, Pot.S
  N3: 555.OUT, R2.Pin_1
  N4: 555._RES, 555.VCC+, C3.+, motor.pin_2, R1.Pin_0, M.2, button.leg1, B.2, Reg5V.Vin, D3.cathode
  N5: 555.CON, C2.2
  N6: 555.DIS, D1.cathode, D2.anode, R1.Pin_1
  N7: Pot.A, D1.anode
  N8: Pot.E, D2.cathode
  N9: R2.Pin_0, FET.gate
  N10: C3.-, motor.pin_1, M.1, FET.drain, D3.anode
  GND: button.leg0, B.1, Reg5V.GND, Reg8V.Vin
  N11: DC_jack.center, V.2, Reg8V.GND

notes:
  Reg5V and Reg8V pins are WRONG!!!
  left Vin
  middle GND
  right Vout
  555 Motor Control
  sPring version2
  BOOST
  - carregar no botão envia uma voltagem maior do q 5V (6V?, 8V?, 10V ???)
  - o regulador certifica que não há um excesso de voltagem para o motor
  isto porque os motores podem não arrancar devido ao pêndulo
  L7805
  L7808
  IRF640N
  555
  5.2cm (22p)
  4.9cm (20p)
  WARNING!!!!
  this is a perfboard schematic and not a PCB!

custom parts:
  2.1mm DC Barrel Jack: 2.1mm DC Barrel Jack with Thru-Hole Connectors (breadboardable)
  STP16NF06 N-Channel Power MOSFET: STP16NF06 N-channel Power MOSFET
