# Fritzing sketch 555_String_Motor_Control_v2 (saved by Fritzing 0.9.2b)
circuit board: 5.5cm x 3.75cm
breadboards: 1

parts:
  555 = General purpose bipolar Timer [package=dil-08]
  C1 = Capacitor [package=cap-pth-small2]
  C2 = Capacitor [package=cap-pth-small2]
  JACK1 = 2.1mm DC Barrel Jack
  REG = LD33 Low-Dropout Voltage Regulator
  Pot = POT [package=pot_alpha_rv16af-20]
  D1 = Rectifier Diode [part_number=1N4001 package="300 mil [THT]"]
  D2 = Rectifier Diode [part_number=1N4001 package="300 mil [THT]"]
  R2 = Resistor [tolerance=±5% resistance=1k package="0805 [SMD]"]
  FET = STP16NF06 N-Channel Power MOSFET
  D3 = Rectifier Diode [part_number=1N4001 package="300 mil [THT]"]
  C3 = Electrolytic Capacitor [capacitance=1000µF package="300 mil [THT, electrolytic]"]
  M1 = DC Motor
  V = Header 2 [package=screwterminal-3.5mm-2_lock]
  R1 = Resistor [tolerance=±5% resistance=1k package="0805 [SMD]"]
  M = Header 2 [package=screwterminal-3.5mm-2_lock]

nets:
  N1: 555.GND, C1.1, C2.1, JACK1.sleeve, REG.Vout, FET.source, V.1
  N2: 555.TRI, 555.TRE, C1.2, Pot.S
  N3: 555.OUT, R2.Pin_1
  N4: 555._RES, 555.VCC+, REG.Vin, D3.cathode, C3.+, M1.pin_2, R1.Pin_0, M.2
  N5: 555.CON, C2.2
  N6: 555.DIS, D1.cathode, D2.anode, R1.Pin_1
  N7: JACK1.center, REG.GND, V.2
  N8: Pot.A, D1.anode
  N9: Pot.E, D2.cathode
  N10: R2.Pin_0, FET.gate
  N11: FET.drain, D3.anode, C3.-, M1.pin_1, M.1

notes:
  REG1 pins are WRONG!!!
  left Vin
  middle GND
  right Vout
  555 Motor Control
  sTring version2
  minimum input voltage : 7.3V ??
  maximum output voltage : 5.???
  5.5cm (23p)
  3.75cm (16p)

custom parts:
  2.1mm DC Barrel Jack: 2.1mm DC Barrel Jack with Thru-Hole Connectors (breadboardable)
  STP16NF06 N-Channel Power MOSFET: STP16NF06 N-channel Power MOSFET
